# Fritzing sketch 32u4-programmer (saved by Fritzing 0.9.3b)
breadboards: 1

parts:
  Part1 = Itsy Bitsy 32u4 5V @ 16MHz [part_number="Adafruit #3677"]
  J1 = Piezo Speaker
  U1 = ZIFSOCKET-40-6 [package=dil40-6-zif_socket]
  U2 = ATTINY13 [package=dip]
  U3 = 74HC595 [package="DIP16 [THT]"]
  U4 = 74HC595 [package="DIP16 [THT]"]
  C1 = Electrolytic Capacitor [capacitance=4.7µF voltage=35V package="100 mil [THT, electrolytic]"]
  C2 = Electrolytic Capacitor [capacitance=4.7µF voltage=35V package="100 mil [THT, electrolytic]"]

nets:
  GND: Part1.GND, J1.pin1, U1.P$20, U3.GND, U3.OE, U4.GND, U4.OE, C2.-
  N1: Part1.D7, J1.pin2
  N2: Part1.MISO, U2.PB1(MISO)
  N3: Part1.MOSI, U2.PB0(MOSI)
  N4: Part1.SCK, U2.PB2(SCK_ADC1)
  N5: Part1.A5, U2.PB5(NRES)
  VCC: Part1.+5V, U3.MR, U3.VCC, U4.MR, U4.VCC, C1.+
  N6: U1.P$6, U1.P$35
  N7: U3.Q7', U4.DS
  N8: U3.SH_CP, U4.SH_CP
  N9: U3.ST_CP, U4.ST_CP
  N10: C1.-, C2.+

custom parts:
  Itsy Bitsy 32u4 5V @ 16MHz: What's smaller than a Feather but larger than a Trinket? It's an Itsy Bitsy! Small, powerful, Arduino-compatible - this microcontroller board is perfect when you want something very compact, but still with a bunch of pins. Itsy Bitsy is only 1.4" long by 0.7" wide, but has 6 power pins, 6 analog & digital pins and 17 digital pins. It packs much of the same capability as an Arduino UNO. So it's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
